# Fritzing sketch jeux_schema+code (saved by Fritzing 0.9.3b)
breadboards: 2

parts:
  Composant1 = Arduino Mega 2560 (Rev3)
  SP1 = SPEAKER [package=pcb_mount_speaker]
  LED1 = RGB LED (com. cathode, rgb) [package="5 mm [THT]"]
  LED2 = RGB LED (com. cathode, rgb) [package="5 mm [THT]"]
  LED3 = RGB LED (com. cathode, rgb) [package="5 mm [THT]"]
  LED4 = RGB LED (com. cathode, rgb) [package="5 mm [THT]"]
  R1 = Resistor [tolerance=±5% resistance=220 package=THT]
  R2 = Resistor [tolerance=±5% resistance=220 package=THT]
  R3 = Resistor [tolerance=±5% resistance=220 package=THT]
  R4 = Resistor [tolerance=±5% resistance=220 package=THT]
  R5 = Resistor [tolerance=±5% resistance=220 package=THT]
  R6 = Resistor [tolerance=±5% resistance=220 package=THT]
  R7 = Resistor [tolerance=±5% resistance=220 package=THT]
  R8 = Resistor [tolerance=±5% resistance=220 package=THT]
  R9 = Resistor [tolerance=±5% resistance=220 package=THT]
  R10 = Resistor [tolerance=±5% resistance=220 package=THT]
  R11 = Resistor [tolerance=±5% resistance=220 package=THT]
  R12 = Resistor [tolerance=±5% resistance=220 package=THT]
  LED5 = LED - 5mm [color="Red (633nm)" package="5 mm [THT]"]
  R13 = Resistor [tolerance=±5% resistance=220 package=THT]
  S1 = Pushbutton [package="[THT]"]
  S2 = Pushbutton [package="[THT]"]
  S3 = Pushbutton [package="[THT]"]
  S4 = Pushbutton [package="[THT]"]
  S5 = Pushbutton [package="[THT]"]
  S6 = Pushbutton [package="[THT]"]

nets:
  N1: Composant1.GND, Composant1.D33, Composant1.D37, Composant1.D39, Composant1.D41, SP1.+, LED1.common_cathode, LED2.common_cathode, LED3.common_cathode, LED4.common_cathode, LED5.cathode, S1.Pin_1, S1.Pin_2, S2.Pin_3, S2.Pin_4, S3.Pin_3, S3.Pin_4, S4.Pin_3, S4.Pin_4, S5.Pin_3, S5.Pin_4, S6.Pin_1, S6.Pin_2
  N2: Composant1.D13_PWM, SP1.-
  N3: Composant1.D12_PWM, R4.Pin_1
  N4: Composant1.D11_PWM, R5.Pin_1
  N5: Composant1.D10_PWM, R6.Pin_1
  N6: Composant1.D9_PWM, R7.Pin_1
  N7: Composant1.D8_PWM, R8.Pin_1
  N8: Composant1.D1_TX0, R3.Pin_1
  N9: Composant1.D2_PWM, R2.Pin_1
  N10: Composant1.D3_PWM, R1.Pin_1
  N11: Composant1.D4_PWM, R12.Pin_1
  N12: Composant1.D5_PWM, R11.Pin_1
  N13: Composant1.D6_PWM, R10.Pin_1
  N14: Composant1.D7_PWM, R9.Pin_1
  N15: Composant1.D23, R13.Pin_1
  N16: Composant1.D35, S2.Pin_1, S2.Pin_2
  N17: Composant1.D43, S6.Pin_3, S6.Pin_4
  N18: LED1.red_anode, R4.Pin_0
  N19: LED1.green_anode, R5.Pin_0
  N20: LED1.blue_anode, R6.Pin_0
  N21: LED2.red_anode, R7.Pin_0
  N22: LED2.green_anode, R8.Pin_0
  N23: LED2.blue_anode, R9.Pin_0
  N24: LED3.red_anode, R10.Pin_0
  N25: LED3.green_anode, R11.Pin_0
  N26: LED3.blue_anode, R12.Pin_0
  N27: LED4.red_anode, R1.Pin_0
  N28: LED4.green_anode, R2.Pin_0
  N29: LED4.blue_anode, R3.Pin_0
  N30: LED5.anode, R13.Pin_0
  N31: S1.Pin_3, S1.Pin_4
  N32: S3.Pin_1, S3.Pin_2
  N33: S4.Pin_1, S4.Pin_2
  N34: S5.Pin_1, S5.Pin_2

notes:
  schéma jeux appentissage des couleurs

// code stored in the sketch: code_jeux.ino
#include <SPI.h>
#include <SD.h> // Inclure la librairie SD
#define SDPIN 30 // Chip Select du lecteur SD
#include <TMRpcm.h> 
TMRpcm audio;
File myFile;

int pinbuton1 = 33;
int pinbuton2 = 35;
int pinbuton3 = 37;
int pinbuton4 = 39;
int pinbuton5 = 41;
int pinbuton6 = 43;

/*
 * def pin led RGB
 * 
 * led 1:
 *  R:1
 *  G:2
 *  B:3
 *  
 *  led 2:
 *  R:4
 *  G:5
 *  B:6
 *  
 *  led 3:
 *  R:7
 *  G:8
 *  B:9
 *  
 * led 4:
 *  R:10
 *  G:11
 *  B:12
 *  
 * led 5:
 *  R:13
 *  G:14
 *  B:15
 *  
 */
const byte PIN_LED_ROUGE = 23;

const byte PIN_LED2_R = 4;
const byte PIN_LED2_G = 5;
const byte PIN_LED2_B = 6;

const byte PIN_LED3_R = 7;
const byte PIN_LED3_G = 8;
const byte PIN_LED3_B = 9;

const byte PIN_LED4_R = 10;
const byte PIN_LED4_G = 11;
const byte PIN_LED4_B = 12;

const byte PIN_LED5_R = 13;
const byte PIN_LED5_G = 14;
const byte PIN_LED5_B = 15;

const byte PIN_LED_BLANC = 22;

void setup() {
  // put your setup code here, to run once:
  Serial.begin(9600);

  //initialisation boutons
  pinMode(pinbuton1, INPUT_PULLUP);
  pinMode(pinbuton2, INPUT_PULLUP);
  pinMode(pinbuton3, INPUT_PULLUP);
  pinMode(pinbuton4, INPUT_PULLUP);
  pinMode(pinbuton5, INPUT_PULLUP);
  pinMode(pinbuton6, INPUT_PULLUP);

  //initialisation leds
  pinMode(PIN_LED_ROUGE, OUTPUT);
  pinMode(PIN_LED_BLANC, OUTPUT);
  pinMode(PIN_LED2_R, OUTPUT);
  pinMode(PIN_LED2_G, OUTPUT);
  pinMode(PIN_LED2_B, OUTPUT);
  pinMode(PIN_LED3_R, OUTPUT);
  pinMode(PIN_LED3_G, OUTPUT);
  pinMode(PIN_LED3_B, OUTPUT);
  pinMode(PIN_LED4_R, OUTPUT);
  pinMode(PIN_LED4_G, OUTPUT);
  pinMode(PIN_LED4_B, OUTPUT);
  pinMode(PIN_LED5_R, OUTPUT);
  pinMode(PIN_LED5_G, OUTPUT);
  pinMode(PIN_LED5_B, OUTPUT);
  
  //initialisation de la partie audio
  audio.speakerPin = 13;
  audio.setVolume(4); // gestion du volume de 0 à 7
  audio.quality(1); 

  // Initialisation de la carte SD
  if (!SD.begin(SDPIN)) { 
    Serial.println("initialization failed!"); //  S'il y a un soucis "initialization failed!" s'affichera au moniteur
    return;
  }
}

void loop() {
  // put your main code here, to run repeatedly:
  boolean buton1 = digitalRead(pinbuton1); //rouge
  boolean buton2 = digitalRead(pinbuton2); //bleu
  boolean buton3 = digitalRead(pinbuton3); //vert
  boolean buton4 = digitalRead(pinbuton4); //jaune
  boolean buton5 = digitalRead(pinbuton5); //magenta
  boolean buton6 = digitalRead(pinbuton6); //blanc

  if (buton1 == 1){
    digitalWrite(PIN_LED_ROUGE, HIGH);
    audio.play("sounds/rouge.wav");
    delay(5000);
    digitalWrite(PIN_LED_ROUGE, LOW);
  }
  
  if (buton2 == 1){
    displayColor(0, 0, 255, 2);
    //led bleu
    audio.play("sounds/bleu.wav");
    delay(5000);
    displayColor(0, 0, 0, 2);
  }

  if (buton3 == 1){
    displayColor(0, 255, 0, 3);
    //led vert
    audio.play("sounds/vert.wav");
    delay(5000);
    displayColor(0, 0, 0, 3);
  }

  if (buton4 == 1){
    displayColor(255, 255, 0, 4);
    //led jaune
    audio.play("sounds/jaune.wav");
    delay(5000);
    displayColor(0, 0, 0, 4);
  }

  if (buton5 == 1){
    displayColor(255, 0, 255, 5);
    //led magenta
    audio.play("sounds/magenta.wav");
    delay(5000);
    displayColor(0, 0, 0, 5);
  }

  if (buton6 == 1){
    digitalWrite(PIN_LED_BLANC, HIGH);
    //led blanc
    audio.play("sounds/blanc.wav");
    digitalWrite(PIN_LED_BLANC, LOW);
  }
   
  }

  void displayColor(byte r, byte g, byte b, byte led) {
    // fonction pour l'alumage avec un couleur donné
    if (led == 2){
       analogWrite(PIN_LED2_R, ~r);
       analogWrite(PIN_LED2_G, ~g);
       analogWrite(PIN_LED2_B, ~b);
    }

    if (led == 3){
       analogWrite(PIN_LED2_R, ~r);
       analogWrite(PIN_LED3_G, ~g);
       analogWrite(PIN_LED3_B, ~b);
    }

    if (led == 4){
       analogWrite(PIN_LED4_R, ~r);
       analogWrite(PIN_LED4_G, ~g);
       analogWrite(PIN_LED4_B, ~b);
    }

    if (led == 5){
       analogWrite(PIN_LED5_R, ~r);
       analogWrite(PIN_LED5_G, ~g);
       analogWrite(PIN_LED5_B, ~b);
    }
}
