# Fritzing sketch plaque_bouton (saved by Fritzing 0.9.3b)
circuit board: 8.46667cm x 5.64444cm
breadboards: 1

parts:
  S1 = Pushbutton [package="[THT]"]
  S2 = Pushbutton [package="[THT]"]
  S3 = Pushbutton [package="[THT]"]
  S4 = Pushbutton [package="[THT]"]
  S5 = Pushbutton [package="[THT]"]
  S6 = Pushbutton [package="[THT]"]
  R2 = Resistor [tolerance=±5% resistance=10k package=THT]
  R3 = Resistor [tolerance=±5% resistance=10k package=THT]
  R4 = Resistor [tolerance=±5% resistance=10k package=THT]
  R5 = Resistor [tolerance=±5% resistance=10k package=THT]
  R6 = Resistor [tolerance=±5% resistance=10k package=THT]
  JP3 = FTDI_BASIC [package=ftdi_basic]
  JP4 = FTDI_BASIC [package=ftdi_basic]
  R1 = Resistor [tolerance=±5% resistance=10k package=THT]

nets:
  5V: S1.Pin_1, S1.Pin_2, S2.Pin_1, S2.Pin_2, S3.Pin_1, S3.Pin_2, S4.Pin_1, S4.Pin_2, S5.Pin_1, S5.Pin_2, S6.Pin_1, S6.Pin_2, JP4.3
  N1: S1.Pin_3, S1.Pin_4, JP3.1, R1.Pin_0
  N2: S2.Pin_3, S2.Pin_4, R2.Pin_0, JP3.2
  N3: S3.Pin_3, S3.Pin_4, R3.Pin_0, JP3.3
  N4: S4.Pin_3, S4.Pin_4, R4.Pin_0, JP3.4
  N5: S5.Pin_3, S5.Pin_4, R6.Pin_0, JP3.5
  N6: S6.Pin_3, S6.Pin_4, R5.Pin_0, JP3.6
  GND: R2.Pin_1, R3.Pin_1, R4.Pin_1, R5.Pin_1, R6.Pin_1, JP4.1, R1.Pin_1
