# Fritzing sketch plaque_led (saved by Fritzing 0.9.3b)
circuit board: 8.46667cm x 5.64444cm
breadboards: 1

parts:
  LED1 = LED - 5mm [color="Red (633nm)" package="5 mm [THT]"]
  LED2 = LED - 5mm [color="Orange (612nm)" package="5 mm [THT]"]
  LED3 = LED - 5mm [color="Green (560nm)" package="5 mm [THT]"]
  LED4 = RGB LED (com. cathode, rgb) [package="5 mm [THT]"]
  LED5 = RGB LED (com. cathode, rgb) [package="5 mm [THT]"]
  LED6 = RGB LED (com. cathode, rgb) [package="5 mm [THT]"]
  JP1 = FTDI_BASIC [package=ftdi_basic]
  JP2 = FTDI_BASIC [package=ftdi_basic]
  JP3 = FTDI_BASIC [package=ftdi_basic]

nets:
  N1: LED1.cathode, LED2.cathode, LED3.cathode, LED4.common_cathode, LED5.common_cathode, LED6.common_cathode, JP3.5, JP3.6
  N2: LED1.anode, JP3.2
  N3: LED2.anode, JP3.3
  N4: LED3.anode, JP3.1
  N5: LED4.red_anode, JP1.6
  N6: LED4.green_anode, JP1.5
  N7: LED4.blue_anode, JP1.4
  N8: LED5.red_anode, JP1.3
  N9: LED5.green_anode, JP1.2
  N10: LED5.blue_anode, JP1.1
  N11: LED6.red_anode, JP2.4
  N12: LED6.green_anode, JP2.3
  N13: LED6.blue_anode, JP2.2
